// Digital circuit 1bALU.dig as structural Verilog
module _1bALU (
  input  Invert_A,
  input  Invert_B,
  input  A,
  input  B,
  input  Carry_In,
  input  Invert_Z,
  output Carry_Out,
  output Sum,
  output Z
);

  wire and_1_out, and_2_out, xor_1_out, xor_2_out, xor_3_out;

  xor xor_1 (xor_1_out, Invert_A, A);
  xor xor_2 (xor_2_out, Invert_B, B);
  xor xor_3 (xor_3_out, xor_1_out, xor_2_out);
  and and_1 (and_1_out, xor_1_out, xor_2_out);
  xor xor_4 (Sum, xor_3_out, Carry_In);
  and and_2 (and_2_out, xor_3_out, Carry_In);
  or or_1 (Carry_Out, and_2_out, and_1_out);
  xor xor_5 (Z, and_1_out, Invert_Z);
endmodule
