// Digital circuit 4bALU.dig as structural Verilog
module _4bALU (
  input  Invert_A,
  input  Invert_B,
  input  [3:0] A,
  input  [3:0] B,
  input  Carry_In,
  input  Invert_Z,
  output Carry_Out,
  output [3:0] Sum,
  output [3:0] Z
);

  wire _1balu_1_carry_out, _1balu_2_carry_out, _1balu_3_carry_out;

  _1bALU _1balu_1 (
    .Invert_A(Invert_A), .Invert_B(Invert_B), .A(A[0]), .B(B[0]), .Carry_In(Carry_In), .Invert_Z(Invert_Z),
    .Carry_Out(_1balu_1_carry_out), .Sum(Sum[0]), .Z(Z[0]));
  _1bALU _1balu_2 (
    .Invert_A(Invert_A), .Invert_B(Invert_B), .A(A[1]), .B(B[1]), .Carry_In(_1balu_1_carry_out),
    .Invert_Z(Invert_Z), .Carry_Out(_1balu_2_carry_out), .Sum(Sum[1]), .Z(Z[1]));
  _1bALU _1balu_3 (
    .Invert_A(Invert_A), .Invert_B(Invert_B), .A(A[2]), .B(B[2]), .Carry_In(_1balu_2_carry_out),
    .Invert_Z(Invert_Z), .Carry_Out(_1balu_3_carry_out), .Sum(Sum[2]), .Z(Z[2]));
  _1bALU _1balu_4 (
    .Invert_A(Invert_A), .Invert_B(Invert_B), .A(A[3]), .B(B[3]), .Carry_In(_1balu_3_carry_out),
    .Invert_Z(Invert_Z), .Carry_Out(Carry_Out), .Sum(Sum[3]), .Z(Z[3]));
endmodule
