// Digital circuit 8bALU.dig as structural Verilog
module _8bALU (
  input  [7:0] A,
  input  [7:0] B,
  input  Invert_A,
  input  Invert_B,
  input  [7:0] Carry_In,
  input  [7:0] Invert_Z,
  input  [7:0] M,
  output [7:0] Output,
  output Carry_Out
);

  wire _4balu_1_p7;
  wire [7:0] _4balu_1_p8, _4balu_1_p9;

  // _4bALU _4balu_1: pin names not known; wires that end beside it: Invert_A, Invert_B, A[3:0], B[3:0], Carry_In, Invert_Z, _4balu_1_p7, _4balu_1_p8[3:0], _4balu_1_p9[3:0]
  // _4bALU _4balu_2: pin names not known; wires that end beside it: Invert_A, Invert_B, A[7:4], B[7:4], _4balu_1_p7, Invert_Z, Carry_Out, _4balu_1_p8[7:4], _4balu_1_p9[7:4]
  Multiplexer #(.Bits(8)) multiplexer_1 (.sel(M[0]), .in_0(_4balu_1_p8), .in_1(_4balu_1_p9), .out(Output));
  // Pins of 1 and 8 bits meet at Output
  // Pins of 1 and 8 bits meet at M
endmodule
