// Digital circuit Main.dig as structural Verilog
module Main (
  input  in_1,
  input  clk
);

  wire _74161_1_p15, and_1_out, and_2_out, and_3_out, Carry_In, decoder_2_out_4, decoder_2_out_5, DS_In,
       DS_Out, DSDown, DSUp, Invert_A, Invert_B, Invert_Z, IR_IN, M, MM_In, MM_Out, MUX, nCLR, Next,
       not_1_out, not_2_out, not_3_out, not_4_out, PC_Enable, PC_Out, PCH_In, PCL_In, TOS_IN, TOS_Out;
  wire [2:0] _74161_1_p12;
  wire [7:0] _8balu_1_p8, _74574_2_p19, DataBus, multiplexer_1_out, stackaddressgen_1_address;
  wire [10:3] _74574_1_p20;
  wire [14:8] eeprom_1_d;
  wire [15:0] AddressBus;

  and and_1 (and_1_out, ~Next, nCLR, ~_74161_1_p15);  // And
  and and_2 (and_2_out, clk, IR_IN);
  Reset reset_1 (.out(nCLR));
  not not_1 (not_1_out, clk);
  not not_2 (not_2_out, in_1);
  // _74574 _74574_1: pin names not known; wires that end beside it: 1'b0, and_2_out, DataBus[0], DataBus[1], DataBus[2], DataBus[3], DataBus[4], DataBus[5], DataBus[6], DataBus[7], 1'b1, 1'b0, _74574_1_p20[3], _74574_1_p20[4], _74574_1_p20[5], _74574_1_p20[6], _74574_1_p20[7], _74574_1_p20[8], _74574_1_p20[9], _74574_1_p20[10]
  // _74161 _74161_1: pin names not known; wires that end beside it: 1'b1, and_1_out, not_1_out, 1'b1, not_2_out, 1'b0, 1'b0, 1'b0, 1'b0, 1'b1, 1'b0, _74161_1_p12[0], _74161_1_p12[1], _74161_1_p12[2], _74161_1_p15
  // Probe on {_74574_1_p20, _74161_1_p12}
  EEPROM #(.AddrBits(11), .Bits(16)) eeprom_1 (
    .A({_74574_1_p20, _74161_1_p12}), .CS(1'b1), .WE(1'b0), .OE(1'b1),
    .D({Next, eeprom_1_d, MUX, Invert_A, Invert_B, Carry_In, Invert_Z, M, PC_Enable, PC_Out}));
  // Probe on AddressBus
  EEPROM #(.AddrBits(16), .Bits(8)) eeprom_2 (.A(AddressBus), .CS(1'b1), .WE(MM_In), .OE(MM_Out), .D(DataBus));
  not not_3 (not_3_out, PCL_In);
  not not_4 (not_4_out, PCH_In);
  Decoder #(.Selector_Bits(3)) decoder_1 (
    .sel(eeprom_1_d[10:8]), .out_1(TOS_IN), .out_2(PCH_In), .out_3(PCL_In), .out_4(IR_IN), .out_5(DS_In),
    .out_6(MM_In));  // open: out_0, out_7
  // Probe on DataBus
  PC pc_1 (
    .DataBus(DataBus), .CountUp(PC_Enable), .nCLR(nCLR), .CLK(clk), .nLD_Low(not_3_out),
    .nLD_High(not_4_out), .OE(PC_Out), .Address(AddressBus));
  Decoder #(.Selector_Bits(3)) decoder_2 (
    .sel(eeprom_1_d[13:11]), .out_1(DS_Out), .out_2(TOS_Out), .out_3(MM_Out), .out_4(decoder_2_out_4),
    .out_5(decoder_2_out_5));  // open: out_0, out_6, out_7
  not not_5 (DSUp, decoder_2_out_4);
  not not_6 (DSDown, decoder_2_out_5);
  Multiplexer #(.Bits(8)) multiplexer_1 (.sel(MUX), .in_0(_8balu_1_p8), .in_1(DataBus), .out(multiplexer_1_out));
  and and_3 (and_3_out, TOS_IN, clk);
  // _74574 _74574_2: pin names not known; wires that end beside it: 1'b0, and_3_out, multiplexer_1_out[0], multiplexer_1_out[1], multiplexer_1_out[2], multiplexer_1_out[3], multiplexer_1_out[4], multiplexer_1_out[5], multiplexer_1_out[6], multiplexer_1_out[7], 1'b1, 1'b0, _74574_2_p19[0], _74574_2_p19[1], _74574_2_p19[2], _74574_2_p19[3], _74574_2_p19[4], _74574_2_p19[5], _74574_2_p19[6], _74574_2_p19[7]
  StackAddressGen stackaddressgen_1 (
    .Down(DSDown), .Up(DSUp), .CLR(nCLR), .Address(stackaddressgen_1_address));  // open: nUnderflow, nOverflow
  assign DataBus = TOS_Out ? _74574_2_p19 : 8'bz;  // Driver driver_1
  // Probe on stackaddressgen_1_address
  RAMSinglePortSel #(.AddrBits(8), .Bits(8)) ramsingleportsel_1 (
    .A(stackaddressgen_1_address), .CS(1'b1), .WE(DS_In), .OE(DS_Out), .D(DataBus));
  // _8bALU _8balu_1: pin names not known; wires that end beside it: _74574_2_p19, DataBus, Invert_A, Invert_B, Carry_In, Invert_Z, M, _8balu_1_p8
  PullDown #(.Bits(8)) pulldown_1 (.out(DataBus));

  // Other names for the same wires on the sheet: HALT = in_1

  // Notes on the sheet:
  //   clk: Hz: 20
  //   contents of eeprom_1 (hex, n*v repeats v):
  //   1c03,7*0,1c03,2000,1500,1983,8000,0,0,0,1c03,900,a800,5*0,1c03
  //   ,1a03,1b03,8000,5,6,7,8
  //   contents of eeprom_2 (hex, n*v repeats v):
  //   0,1,1,2,3,0,0,22,3
endmodule
