// Digital circuit PC.dig as structural Verilog
module PC (
  input  [7:0] DataBus,
  input  CountUp,
  input  nCLR,
  input  CLK,
  input  nLD_Low,
  input  nLD_High,
  input  OE,
  output [15:0] Address
);

  wire _74161_1_p12, _74161_2_p12, _74161_3_p12;
  wire [3:0] _74161_1_p13, _74161_2_p13, _74161_3_p13, _74161_4_p12;

  // _74161 _74161_1: pin names not known; wires that end beside it: nLD_Low, nCLR, CLK, 1'b1, CountUp, DataBus[0], DataBus[1], DataBus[2], DataBus[3], 1'b1, 1'b0, _74161_1_p12, _74161_1_p13[0], _74161_1_p13[1], _74161_1_p13[2], _74161_1_p13[3]
  // _74161 _74161_2: pin names not known; wires that end beside it: nLD_Low, nCLR, CLK, _74161_1_p12, CountUp, DataBus[4], DataBus[5], DataBus[6], DataBus[7], 1'b1, 1'b0, _74161_2_p12, _74161_2_p13[0], _74161_2_p13[1], _74161_2_p13[2], _74161_2_p13[3]
  // _74161 _74161_3: pin names not known; wires that end beside it: nLD_High, nCLR, CLK, _74161_2_p12, CountUp, DataBus[0], DataBus[1], DataBus[2], DataBus[3], 1'b1, 1'b0, _74161_3_p12, _74161_3_p13[0], _74161_3_p13[1], _74161_3_p13[2], _74161_3_p13[3]
  // _74161 _74161_4: pin names not known; wires that end beside it: nLD_High, nCLR, CLK, _74161_3_p12, CountUp, DataBus[4], DataBus[5], DataBus[6], DataBus[7], 1'b1, 1'b0, _74161_4_p12[0], _74161_4_p12[1], _74161_4_p12[2], _74161_4_p12[3]
  assign Address = OE ? {_74161_4_p12, _74161_3_p13, _74161_2_p13, _74161_1_p13} : 16'bz;  // Driver driver_1

  // Other names for the same wires on the sheet: Enable = CountUp; nLD = nLD_Low; nLDH = nLD_High
endmodule
