// Digital circuit StackAddressGen.dig as structural Verilog
module StackAddressGen (
  input  Down,
  input  Up,
  input  nCLR,
  output nUnderflow,
  output nOverflow,
  output [7:0] Address
);

  wire Borrow_Out, Carry_Out, CLR;

  not not_1 (CLR, nCLR);
  // _74193 _74193_1: pin names not known; wires that end beside it: Down, Up, 1'b0, 1'b0, 1'b0, 1'b0, CLR, 1'b1, 1'b1, 1'b0, Borrow_Out, Carry_Out, Address[0], Address[1], Address[2], Address[3]
  // _74193 _74193_2: pin names not known; wires that end beside it: Borrow_Out, Carry_Out, 1'b0, 1'b0, 1'b0, 1'b0, CLR, 1'b1, 1'b1, 1'b0, nUnderflow, nOverflow, Address[4], Address[5], Address[6], Address[7]
endmodule
